# Fritzing sketch Projektna (saved by Fritzing 0.9.5d)
breadboards: 1

parts:
  Arduino = Arduino Uno (Rev3)
  S1 = Pushbutton [package="[THT]"]
  S2 = Pushbutton [package="[THT]"]
  S3 = Pushbutton [package="[THT]"]
  S4 = Pushbutton [package="[THT]"]
  LED1 = LED - 5mm [color="Green (570nm)" package="5 mm [THT]"]  # not connected
  M1 = DC Motor  # not connected
  R1 = Resistor [tolerance=±5% resistance=1k package=THT]
  R2 = Resistor [tolerance=±5% resistance=1k package=THT]
  R3 = Resistor [tolerance=±5% resistance=1k package=THT]
  R4 = Resistor [tolerance=±5% resistance=1k package=THT]
  D1 = Rectifier Diode [part_number=1N4001 package="300 mil [THT]"]  # not connected

nets:
  GND: Arduino.GND, R1.Pin_1, R2.Pin_1, R3.Pin_1, R4.Pin_1
  N1: Arduino.5V, S1.Pin_3, S1.Pin_4, S2.Pin_3, S2.Pin_4, S3.Pin_3, S3.Pin_4, S4.Pin_3, S4.Pin_4
  N2: S1.Pin_1, R1.Pin_0
  N3: S2.Pin_1, S2.Pin_2, R2.Pin_0
  N4: S3.Pin_1, S3.Pin_2, R3.Pin_0
  N5: S4.Pin_1, S4.Pin_2, R4.Pin_0
